// Logisim project gol_16.circ as structural Verilog: 4 circuits, main circuit gol16
module gol16 (
);

  wire clk, clr, frce, froe, iclk, t1ce, t2ce, t2oe;
  wire [3:0] alu_1_c;
  wire [15:0] alu_1_r, reg16_1_q, reg16_2_q;

  Button button_1 (.out(clr));
  Clock clock_1 (.out(clk));
  not not_1 (iclk, clk);
  reg16 reg16_1 (.OE(t2ce), .CE(t1ce), .CLK(iclk), .CLR(clr), .Q(reg16_1_q));  // open: D
  alu alu_1 (
    .A(reg16_1_q), .Z(alu_1_c[3]), .C(alu_1_c[0]), .V(alu_1_c[1]), .N(alu_1_c[2]), .R(alu_1_r));  // open: Op, B
  reg16 reg16_2 (.OE(t2oe), .CE(t2ce), .CLK(iclk), .D(alu_1_r), .CLR(clr), .Q(reg16_2_q));
  reg4 reg4_1 (.OE(froe), .CE(frce), .CLK(iclk), .D(alu_1_c), .CLR(clr));  // open: Q
endmodule

module alu (
  input  [3:0] Op,
  input  [15:0] A,
  input  [15:0] B,
  output [15:0] R,
  output Z,
  output C,
  output V,
  output N
);

  wire addc, or_3_out, or_4_out, seventeen_out, subb, zero_out;
  wire [2:0] divf, mulf;
  wire [2:1] addf, subf;
  wire [4:0] bitadder_1_out;
  wire [7:0] divq, divrem;
  wire [14:0] addr, divr, mulr, subr;
  wire [15:0] and_1_out, mulc, mulv, not_1_out, or_1_out, shifter_1_out, shifter_2_out, shifter_3_out,
       shifter_4_out;

  Multiplier #(.mode("twosComplement"), .width(16)) multiplier_1 (.a(A), .b(B), .cout(mulv));  // open: out, cin
  xor xor_1 (addf[1], addc, addf[2]);
  xor xor_2 (subf[1], subb, subf[2]);
  Adder #(.width(16)) adder_1 (.a(A), .b(B), .out({addf[2], addr}), .cin(1'b0), .cout(addc));
  Subtractor #(.width(16)) subtractor_1 (.a(B), .b(B), .out({subf[2], subr}), .bin(1'b0), .bout(subb));
  Multiplier #(.width(16)) multiplier_2 (.a(A), .b(B), .out({mulf[2], mulr}), .cout(mulc));  // open: cin
  Divider #(.width(16)) divider_1 (
    .a(A), .b(B), .out({divq, divr[7:0]}), .rem({divrem, divf[2], divr[14:8]}));  // open: upper
  assign and_1_out = A & B;  // AND_Gate and_1, 16 bits wide
  assign or_1_out = A | B;  // OR_Gate or_1, 16 bits wide
  assign not_1_out = ~B;  // NOT_Gate not_1, 16 bits wide
  Shifter #(.width(16)) shifter_1 (.in(A), .\dist (B[3:0]), .out(shifter_1_out));
  Shifter #(.shift("lr"), .width(16)) shifter_2 (.in(A), .\dist (B[3:0]), .out(shifter_2_out));
  Shifter #(.shift("rl"), .width(16)) shifter_3 (.in(A), .\dist (B[3:0]), .out(shifter_3_out));
  Shifter #(.shift("rr"), .width(16)) shifter_4 (.in(A), .\dist (B[3:0]), .out(shifter_4_out));
  BitAdder #(.width(17)) bitadder_1 (.in0({mulv, mulf[2]}), .out(bitadder_1_out));
  or or_2 (mulf[0], mulc[7], mulc[0], mulc[1], mulc[2], mulc[3], mulc[4], mulc[5], mulc[6], mulc[8], mulc[9], mulc[10], mulc[11], mulc[12], mulc[13], mulc[14], mulc[15]);
  and seventeen (seventeen_out, bitadder_1_out[0], ~bitadder_1_out[1], ~bitadder_1_out[2], ~bitadder_1_out[3], bitadder_1_out[4]);  // AND_Gate
  nor zero (zero_out, bitadder_1_out[0], bitadder_1_out[1], bitadder_1_out[2], bitadder_1_out[3], bitadder_1_out[4]);
  nor nor_1 (mulf[1], seventeen_out, zero_out);
  Multiplexer #(.select(4), .width(16)) multiplexer_1 (
    .in0({16{1'b0}}), .in1({addf[2], addr}), .in2({subf[2], subr}), .in3({mulf[2], mulr}),
    .in4({divf[2], divr}), .in5(and_1_out), .in6(or_1_out), .in7(not_1_out), .in8(shifter_1_out),
    .in9(shifter_2_out), .in10(shifter_3_out), .in11(shifter_4_out), .out(R), .sel(Op));  // open: in12, in13, in14, in15
  or or_3 (or_3_out, divq[3], divq[0], divq[1], divq[2], divq[4], divq[5], divq[6], divq[7]);
  or or_4 (or_4_out, divrem[3], divrem[0], divrem[1], divrem[2], divrem[4], divrem[5], divrem[6], divrem[7]);
  or or_5 (divf[0], or_3_out, or_4_out);
  Multiplexer #(.select(4), .width(3)) multiplexer_2 (
    .in0(3'b000), .in1({addf, addc}), .in2({subf, subb}), .in3(mulf), .in4({divf[2], 1'b0, divf[0]}),
    .in5(3'b000), .in6(3'b000), .in7(3'b000), .in8(3'b000), .in9(3'b000), .in10(3'b000), .in11(3'b000),
    .out({N, V, C}), .sel(Op));  // open: in12, in13, in14, in15
  nor nor_2 (Z, R[15], R[14], R[13], R[12], R[11], R[10], R[9], R[8], R[7], R[6], R[5], R[4], R[3], R[2], R[1], R[0]);

  // Other names for the same wires on the sheet: addf[0] = addc; addr[15] = addf[2]; divr[15] = divf[2];
  //   mulr[15] = mulf[2]; oper[3:0] = Op; subf[0] = subb; subr[15] = subf[2]

  // Notes on the sheet:
  //   Single source operations use B
  //   Add flag generator
  //   Sub flag generator
  //   Detects if any of the 2's compliment multiplication bits + the MSB of the result are different (XOR)
  //   Logisim XOR used voting behaviour which was not desirable
  //   8b remainder 8b quotient, remainder stored in MSBs
  //   Multiplication flag generator
  //   No operation
  //   Division flag generator
  //   Result MUX
  //   Signed division can be implemented in software by correcting for (negating output appropriately) the signs of the two operands
  //   Due to the complexity of signed division, this ALU will only perform unsigned division (hence 0 for V flag)
  //   Flag MUX
endmodule

module reg16 (
  input  [15:0] D,
  input  CE,
  input  OE,
  input  CLK,
  input  CLR,
  output [15:0] Q
);

  wire [15:0] register_1_q;

  Register #(.width(16)) register_1 (.D(D), .en(CE), .clk(CLK), .Q(register_1_q), .clr(CLR));
  assign Q = OE ? register_1_q : 16'bz;  // Controlled_Buffer controlled_buffer_1
endmodule

module reg4 (
  input  [3:0] D,
  input  CE,
  input  OE,
  input  CLK,
  input  CLR,
  output [3:0] Q
);

  wire [3:0] register_1_q;

  Register #(.width(4)) register_1 (.D(D), .en(CE), .clk(CLK), .Q(register_1_q), .clr(CLR));
  assign Q = OE ? register_1_q : 4'bz;  // Controlled_Buffer controlled_buffer_1
endmodule
